# Fritzing sketch RPS1 (saved by Fritzing 0.9.3b)
breadboards: 1

parts:
  BAT1 = Battery Holders [package=battcon_12mm]
  LED1 = RGB LED - (4 legs) [package="5 mm [THT]"]
  S1 = Pushbutton [package="[THT]"]
  S2 = Pushbutton [package="[THT]"]
  S3 = Pushbutton [package="[THT]"]
  D1 = LTE-302 [package=lte-302]
  D2 = LTE-302 [package=lte-302]
  BR1 = Resistor [tolerance=±5% resistance=220 package=THT]
  BR2 = Resistor [tolerance=±5% resistance=220 package=THT]
  R4 = Resistor [tolerance=±5% resistance=10 package=THT]
  R6 = Resistor [tolerance=±5% resistance=10 package=THT]
  R5 = Resistor [tolerance=±5% resistance=220 package=THT]
  R7 = Resistor [tolerance=±5% resistance=22k package=THT]
  D3 = Rectifier Diode [part_number=1N4001 package="300 mil [THT]"]
  BR3 = Resistor [tolerance=±5% resistance=220 package=THT]
  RPS_Extreme = Arduino Nano (Rev3.0)
  S4 = Pushbutton [package="[THT]"]
  BRR = Resistor [tolerance=±5% resistance=220 package=THT]
  IC1 = IC, DIP package, 6 pins [chip_label=IC]  # not connected

nets:
  N1: BAT1.+, S1.Pin_3, S1.Pin_4, S2.Pin_1, S2.Pin_2, S3.Pin_1, S3.Pin_2, RPS_Extreme.3V3, S4.Pin_3, S4.Pin_4
  N2: BAT1.-, LED1.green_cathode, D1.A, BR1.Pin_1, BR2.Pin_1, D3.cathode, BR3.Pin_1, RPS_Extreme.GND, BRR.Pin_1
  N3: LED1.red_cathode, R4.Pin_1
  N4: LED1.common_anode, R5.Pin_1
  N5: LED1.blue_cathode, R6.Pin_1
  N6: S1.Pin_1, S1.Pin_2, BR1.Pin_0, RPS_Extreme.D4
  N7: S2.Pin_3, S2.Pin_4, BR2.Pin_0, RPS_Extreme.D5
  N8: S3.Pin_3, S3.Pin_4, BR3.Pin_0, RPS_Extreme.D6
  N9: D1.C, RPS_Extreme.D11/MOSI
  N10: D2.A, R7.Pin_0, RPS_Extreme.A1
  N11: D2.C, RPS_Extreme.D10
  N12: R4.Pin_0, RPS_Extreme.D7
  N13: R6.Pin_0, RPS_Extreme.D9
  N14: R5.Pin_0, RPS_Extreme.D8
  N15: R7.Pin_1, D3.anode
  N16: RPS_Extreme.D3, S4.Pin_1, S4.Pin_2, BRR.Pin_0

// code stored in the sketch: RPS.ino
#define BTN_ROCK 3
#define BTN_PAPER 4
#define BTN_SCISSORS 5

#define RED_PIN 8
#define GREEN_PIN 7
#define BLUE_PIN 6


void setup() {
  while (!Serial);
  Serial.begin(115200);
  
  pinMode(BTN_ROCK, INPUT);
  pinMode(BTN_PAPER, INPUT);
  pinMode(BTN_SCISSORS, INPUT);
  
  pinMode(RED_PIN, OUTPUT);
  pinMode(GREEN_PIN, OUTPUT);
  pinMode(BLUE_PIN, OUTPUT);

  Serial.println("SETUP Complete");
}

void loop() {
  if(digitalRead(BTN_ROCK) == HIGH){
    Serial.println("ROCK");
    digitalWrite(RED_PIN, HIGH);
  }

  if(digitalRead(BTN_PAPER) == HIGH){
    Serial.println("PAPER");
    digitalWrite(GREEN_PIN, HIGH);
  }

  if(digitalRead(BTN_SCISSORS) == HIGH){
    Serial.println("SCISSORS");
    digitalWrite(BLUE_PIN, HIGH);
  }

  delay(100);
  digitalWrite(RED_PIN, LOW);
  digitalWrite(GREEN_PIN, LOW);
  digitalWrite(BLUE_PIN, LOW);
}
