# Fritzing sketch RPS2 (saved by Fritzing 0.9.3b)
circuit board: 6.4cm x 3cm
breadboards: 1

parts:
  BR5 = Resistor [tolerance=±5% resistance=220 package=THT]
  R4 = Resistor [tolerance=±5% resistance=10 package=THT]
  BR1 = Resistor [tolerance=±5% resistance=220 package=THT]
  IR_OUT = LTE-302 [package=lte-302]
  RPS_Extreme = Arduino Nano (Rev3.0)
  BR2 = Resistor [tolerance=±5% resistance=220 package=THT]
  BRR = Resistor [tolerance=±5% resistance=220 package=THT]
  R6 = Resistor [tolerance=±5% resistance=10 package=THT]
  R5 = Resistor [tolerance=±5% resistance=220 package=THT]
  BR3 = Resistor [tolerance=±5% resistance=220 package=THT]
  R7 = Resistor [tolerance=±5% resistance=22k package=THT]
  D3 = Rectifier Diode [part_number=1N4001 package="300 mil [THT]"]
  LED1 = RGB LED - (4 legs) [package="5 mm [THT]"]
  BAT1 = Battery Holders [package=battcon_12mm]
  IC1 = IC, DIP package, 6 pins [chip_label=IC]
  IR_IN = LTE-302 [package=lte-302]

nets (from the breadboard view):
  N1: BR5.Pin_0, IC1.pin4
  N2: BR5.Pin_1, BR1.Pin_1, IR_OUT.A, RPS_Extreme.GND, BR2.Pin_1, BRR.Pin_1, BR3.Pin_1, D3.cathode, LED1.green_cathode, BAT1.-
  N3: R4.Pin_0, RPS_Extreme.D6
  N4: R4.Pin_1, LED1.red_cathode
  N5: BR1.Pin_0, IC1.pin1
  N6: IR_OUT.C, RPS_Extreme.D2
  N7: RPS_Extreme.D3, IR_IN.C
  N8: RPS_Extreme.D4, R6.Pin_0
  N9: RPS_Extreme.D5, R5.Pin_0
  N10: RPS_Extreme.VIN, BAT1.+, IC1.pin5
  N11: RPS_Extreme.A1, R7.Pin_0, IR_IN.A
  N12: BR2.Pin_0, IC1.pin2
  N13: BRR.Pin_0, IC1.pin6
  N14: R6.Pin_1, LED1.blue_cathode
  N15: R5.Pin_1, LED1.common_anode
  N16: BR3.Pin_0, IC1.pin3
  N17: R7.Pin_1, D3.anode

// code stored in the sketch: RPS.ino
#define BTN_ROCK 3
#define BTN_PAPER 4
#define BTN_SCISSORS 5

#define RED_PIN 8
#define GREEN_PIN 7
#define BLUE_PIN 6


void setup() {
  while (!Serial);
  Serial.begin(115200);
  
  pinMode(BTN_ROCK, INPUT);
  pinMode(BTN_PAPER, INPUT);
  pinMode(BTN_SCISSORS, INPUT);
  
  pinMode(RED_PIN, OUTPUT);
  pinMode(GREEN_PIN, OUTPUT);
  pinMode(BLUE_PIN, OUTPUT);

  Serial.println("SETUP Complete");
}

void loop() {
  if(digitalRead(BTN_ROCK) == HIGH){
    Serial.println("ROCK");
    digitalWrite(RED_PIN, HIGH);
  }

  if(digitalRead(BTN_PAPER) == HIGH){
    Serial.println("PAPER");
    digitalWrite(GREEN_PIN, HIGH);
  }

  if(digitalRead(BTN_SCISSORS) == HIGH){
    Serial.println("SCISSORS");
    digitalWrite(BLUE_PIN, HIGH);
  }

  delay(100);
  digitalWrite(RED_PIN, LOW);
  digitalWrite(GREEN_PIN, LOW);
  digitalWrite(BLUE_PIN, LOW);
}
