# Fritzing sketch RPS3.2 (saved by Fritzing 0.9.3b)
circuit board: 7cm x 2.6cm
breadboards: 1

parts:
  RB4 = Resistor [tolerance=±5% resistance=220 package=THT]
  RB5 = Resistor [tolerance=±5% resistance=220 package=THT]
  RB1 = Resistor [tolerance=±5% resistance=220 package=THT]
  RB2 = Resistor [tolerance=±5% resistance=220 package=THT]
  RB3 = Resistor [tolerance=±5% resistance=220 package=THT]
  Part1 = Arduino Nano (Rev3.0)
  LED = RGB LED - (4 legs) [package="5 mm [THT]"]
  RLED1 = Resistor [tolerance=±5% resistance=10 package=THT]
  RLED2 = Resistor [tolerance=±5% resistance=220 package=THT]
  RLED3 = Resistor [tolerance=±5% resistance=10 package=THT]
  IR_IN = LTE-302 [package=lte-302]
  IR_OUT = LTE-302 [package=lte-302]
  R1 = Resistor [tolerance=±5% resistance=1k package=THT]
  D1 = Rectifier Diode [part_number=1N4001 package="300 mil [THT]"]
  BTN = IC, DIP package, 6 pins [chip_label=IC]
  BATT = Battery Holders [package=battcon_12mm]
  RLED4 = Resistor [tolerance=±5% resistance=47k package=THT]

nets:
  N1: RB4.Pin_0, RB5.Pin_0, RB1.Pin_0, RB2.Pin_0, RB3.Pin_0, Part1.GND, LED.green_cathode, IR_OUT.A, D1.cathode, BATT.-
  N2: RB4.Pin_1, Part1.D2, BTN.pin6
  N3: RB5.Pin_1, Part1.D3, BTN.pin5
  N4: RB1.Pin_1, Part1.D12/MISO, BTN.pin1
  N5: RB2.Pin_1, Part1.D11/MOSI, BTN.pin2
  N6: RB3.Pin_1, Part1.D10, BTN.pin3
  N7: Part1.D5, RLED1.Pin_0
  N8: Part1.D6, RLED2.Pin_0
  N9: Part1.D7, RLED3.Pin_0
  N10: Part1.D8, IR_OUT.C
  N11: Part1.D9, IR_IN.C
  VIN: Part1.VIN, Part1.3V3, BTN.pin4, BATT.+
  N12: Part1.A7, IR_IN.A, R1.Pin_0
  N13: Part1.A6, RLED4.Pin_0
  N14: LED.red_cathode, RLED1.Pin_1
  N15: LED.common_anode, RLED2.Pin_1, RLED4.Pin_1
  N16: LED.blue_cathode, RLED3.Pin_1
  N17: R1.Pin_1, D1.anode

notes:
  TEXT HERE
