# Fritzing sketch RPS3.4 (saved by Fritzing 0.9.3b)
circuit board: 8.5cm x 3.6cm
breadboards: 1

parts:
  RB6 = Resistor [tolerance=±5% resistance=1k package=THT]
  RB5 = Resistor [tolerance=±5% resistance=1k package=THT]
  RB1 = Resistor [tolerance=±5% resistance=1k package=THT]
  RB2 = Resistor [tolerance=±5% resistance=1k package=THT]
  RB3 = Resistor [tolerance=±5% resistance=1k package=THT]
  Part1 = Arduino Nano (Rev3.0)
  LED = RGB LED - (4 legs) [package="5 mm [THT]"]
  RLED1 = Resistor [tolerance=±5% resistance=220 package=THT]
  RLED2 = Resistor [tolerance=±5% resistance=1k package=THT]
  RLED3 = Resistor [tolerance=±5% resistance=220 package=THT]
  IR_IN = LTE-302 [package=lte-302]
  IR_OUT = LTE-302 [package=lte-302]
  R1 = Resistor [tolerance=±5% resistance=1k package=THT]
  RLED4 = Resistor [tolerance=±5% resistance=47k package=THT]
  BATT2 = Battery Holders [package=battcon_20mm_4legs]
  BATT1 = Battery Holders [package=battcon_20mm_4legs]
  R2 = Resistor [tolerance=±5% resistance=0 package=THT]
  BTN = IC, DIP package, 6 pins [chip_label=IC]
  D1 = Diode [package=diode-1n4001]
  S1 = SPST Switch [package=switch-spst-smd-a]
  Pad1 = Pad [width=8.5590302727877603 height=3.8206287425149688 connect=center]
  Pad2 = Pad [width=8.5590302727877603 height=3.8206287425149688 connect=center]

nets:
  N1: RB6.Pin_0, RB5.Pin_0, RB1.Pin_0, RB2.Pin_0, RB3.Pin_0, Part1.GND, LED.green_cathode, IR_OUT.A, BATT2.-, D1.C
  N2: RB6.Pin_1, Part1.D2, BTN.pin6
  N3: RB5.Pin_1, Part1.D3, BTN.pin5
  N4: RB1.Pin_1, Part1.D12/MISO, BTN.pin1
  N5: RB2.Pin_1, Part1.D11/MOSI, BTN.pin2
  N6: RB3.Pin_1, Part1.D10, BTN.pin3
  N7: Part1.D1/TX, Pad2.pad
  N8: Part1.D0/RX, Pad1.pad
  N9: Part1.D5, RLED1.Pin_0
  N10: Part1.D6, RLED2.Pin_0
  N11: Part1.D7, RLED3.Pin_0
  N12: Part1.D8, R2.Pin_1
  N13: Part1.D9, IR_IN.C
  N14: Part1.VIN, S1.S
  N15: Part1.5V, BTN.pin4
  N16: Part1.A7, IR_IN.A, R1.Pin_0
  N17: Part1.A6, RLED4.Pin_0
  N18: LED.red_cathode, RLED1.Pin_1
  N19: LED.common_anode, RLED2.Pin_1, RLED4.Pin_1
  N20: LED.blue_cathode, RLED3.Pin_1
  N21: IR_OUT.C, R2.Pin_0
  N22: R1.Pin_1, D1.A
  N23: BATT2.+, BATT1.-
  N24: BATT1.+, S1.P

notes:
  4
  MV*
