# Fritzing sketch RPS3 (saved by Fritzing 0.9.3b)
circuit board: 6.2cm x 2.60155cm
breadboards: 1

parts:
  IC1 = IC, DIP package, 6 pins [chip_label=IC]
  RB4 = Resistor [tolerance=±5% resistance=220 package=THT]
  RB5 = Resistor [tolerance=±5% resistance=220 package=THT]
  RB1 = Resistor [tolerance=±5% resistance=220 package=THT]
  RB2 = Resistor [tolerance=±5% resistance=220 package=THT]
  RB3 = Resistor [tolerance=±5% resistance=220 package=THT]
  Part1 = Arduino Nano (Rev3.0)
  LED1 = RGB LED - (4 legs) [package="5 mm [THT]"]
  RLED1 = Resistor [tolerance=±5% resistance=220 package=THT]
  RLED2 = Resistor [tolerance=±5% resistance=220 package=THT]
  RLED3 = Resistor [tolerance=±5% resistance=220 package=THT]
  IR_IN = LTE-302 [package=lte-302]
  IR_OUT = LTE-302 [package=lte-302]
  R1 = Resistor [tolerance=±5% resistance=220 package=THT]
  D1 = Rectifier Diode [part_number=1N4001 package="300 mil [THT]"]
  BATT = Battery Holders [package=battcon_12mm]

nets:
  N1: IC1.pin1, RB1.Pin_1, Part1.D12/MISO
  N2: IC1.pin2, RB2.Pin_1, Part1.D11/MOSI
  N3: IC1.pin3, RB3.Pin_1, Part1.D10
  VIN: IC1.pin4, Part1.VIN, Part1.3V3, BATT.+
  N4: IC1.pin5, RB5.Pin_1, Part1.D3
  N5: IC1.pin6, RB4.Pin_1, Part1.D2
  N6: RB4.Pin_0, RB5.Pin_0, RB1.Pin_0, RB2.Pin_0, RB3.Pin_0, Part1.GND, LED1.green_cathode, IR_OUT.A, D1.cathode, BATT.-
  N7: Part1.D5, RLED1.Pin_0
  N8: Part1.D6, RLED2.Pin_0
  N9: Part1.D7, RLED3.Pin_0
  N10: Part1.D8, IR_OUT.C
  N11: Part1.D9, IR_IN.C
  N12: LED1.red_cathode, RLED1.Pin_1
  N13: LED1.common_anode, RLED2.Pin_1
  N14: LED1.blue_cathode, RLED3.Pin_1
  N15: IR_IN.A, R1.Pin_0
  N16: R1.Pin_1, D1.anode
